# Fritzing sketch IO Breakout (saved by Fritzing 0.9.3b)
circuit board: 3.72761cm x 4.05437cm
breadboards: 1

parts:
  J1 = double row female pin header, 12 pins [form="♀ (female)"]
  J2 = screw terminal, 3 pins
  J3 = screw terminal, 3 pins
  J4 = screw terminal, 6 pins
  J5 = male pin header, 2 pins [form="♂ (male)"]
  J6 = Screw terminal - 2 pins [package=THT]

nets:
  N1: J1.pin1, J2.pin1
  N2: J1.pin2, J4.pin2
  N3: J1.pin3, J4.pin1
  N4: J1.pin4, J3.pin3
  N5: J1.pin5, J3.pin2
  N6: J1.pin6, J3.pin1
  N7: J1.pin7, J4.pin6
  N8: J1.pin8, J4.pin5
  N9: J1.pin9, J4.pin4
  N10: J1.pin10, J4.pin3
  N11: J1.pin11, J2.pin3
  N12: J1.pin12, J2.pin2
  N13: J5.pin1, J6.pin2
  N14: J5.pin2, J6.pin1

notes:
  Gnd
  +3.3V
  +5V
  FAB 001001 ASSY 001001
  CyGate4 I/O Break-out Rev 1.0
  IO16
  IO17
  IO21
  A0
  A1
  A2
  A3
  A4
  A5
  Copyright (c) 2020 Cyrus Brunner
  www.cyrusbuilt.net
  GND
  CyGate4 - I/O Breakout, CyGate4 I/O Break-out adapter, 1.0
  To CyGate4 Conn J23
  To CyGate4 Conn J11
  SDA
  SCL
